# Fritzing sketch ConnectFour (saved by Fritzing 0.9.0b)
breadboards: 2

parts:
  RGB_LED_Matrix1 = RGB LED Matrix (8x8)
  U1 = 74HC595 [package="DIP16 [THT]"]
  U2 = 74HC595 [package="DIP16 [THT]"]  # not connected
  U3 = 74HC595 [package="DIP16 [THT]"]  # not connected
  U4 = 74HC595 [package="DIP16 [THT]"]  # not connected

nets:
  N1: RGB_LED_Matrix1.Pin_17, U1.Q0
  N2: RGB_LED_Matrix1.Pin_18, U1.Q1
  N3: RGB_LED_Matrix1.Pin_19, U1.Q2
  N4: RGB_LED_Matrix1.Pin_20, U1.Q3
  N5: RGB_LED_Matrix1.Pin_29, U1.Q4
  N6: RGB_LED_Matrix1.Pin_30, U1.Q5
  N7: RGB_LED_Matrix1.Pin_31, U1.Q6
  N8: RGB_LED_Matrix1.Pin_32, U1.Q7

custom parts:
  RGB LED Matrix (8x8): Description: This is a large sized, common anode, RGB LED Matrix. This is no supporting intelligence included with this part, so it needs an external driver, for example 4x 74LS595 shift registers and a supporting sketch. Documents: · Datasheet · Supporting info Example Projects: · None yet Dimensions: · 60.5 mm square
