# Fritzing sketch ShiftOut_1 (saved by Fritzing 0.9.0b)
breadboards: 1

parts:
  Part1 = Arduino Uno (Rev3)
  R1 = Resistor [tolerance=±5% resistance=200 package=THT]
  LED1 = LED - 5mm [color="Green (565nm)" package="5 mm [THT]"]
  LED2 = LED - 5mm [color="Green (565nm)" package="5 mm [THT]"]
  R2 = Resistor [tolerance=±5% resistance=200 package=THT]
  LED3 = LED - 5mm [color="Green (565nm)" package="5 mm [THT]"]
  R3 = Resistor [tolerance=±5% resistance=200 package=THT]
  LED4 = LED - 5mm [color="Green (565nm)" package="5 mm [THT]"]
  R4 = Resistor [tolerance=±5% resistance=200 package=THT]
  S1 = Pushbutton [package="[THT]"]
  R5 = Resistor [tolerance=±5% resistance=10k package=THT]
  IC1 = SN74HC595N [package=dil16]
  R6 = Resistor [tolerance=±5% resistance=220 package=THT]  # not connected
  R7 = Resistor [tolerance=±5% resistance=220 package=THT]  # not connected
  R8 = Resistor [tolerance=±5% resistance=68 package=THT]  # not connected

nets:
  N1: Part1.D8, IC1.RCK
  N2: Part1.D11_PWM/MOSI, IC1.SER
  N3: Part1.D12/MISO, IC1.SCK
  GND: Part1.D13/SCK, Part1.GND, R2.Pin_0, R3.Pin_0, R4.Pin_0, S1.Pin_1, S1.Pin_2, S1.Pin_3, S1.Pin_4, R5.Pin_1, IC1.GND, IC1.G
  5V: Part1.5V, R5.Pin_0, IC1.SCL, IC1.VCC
  N4: R1.Pin_1, LED1.cathode
  N5: LED1.anode, IC1.QA
  N6: LED2.cathode, R2.Pin_1
  N7: LED3.cathode, R3.Pin_1
  N8: LED3.anode, IC1.QC
  N9: LED4.cathode, R4.Pin_1
  N10: LED4.anode, IC1.QD

notes:
  This is a test note
  -

custom parts:
  SN74HC595N: 8-bit SHIFT REGISTER, output latch
