# Fritzing sketch Shift_Cascade (saved by Fritzing 0.9.0b)
breadboards: 1

parts:
  LED1 = LED - 5mm [color="Green (570nm)" package="5 mm [THT]"]
  LED2 = LED - 5mm [color="Green (570nm)" package="5 mm [THT]"]
  LED3 = LED - 5mm [color="Green (570nm)" package="5 mm [THT]"]
  LED4 = LED - 5mm [color="Green (570nm)" package="5 mm [THT]"]
  LED5 = LED - 5mm [color="Green (570nm)" package="5 mm [THT]"]
  LED6 = LED - 5mm [color="Green (570nm)" package="5 mm [THT]"]
  LED7 = LED - 5mm [color="Green (570nm)" package="5 mm [THT]"]
  LED8 = LED - 5mm [color="Green (570nm)" package="5 mm [THT]"]
  LED9 = LED - 5mm [color="Red (635nm)" package="5 mm [THT]"]
  LED10 = LED - 5mm [color="Red (635nm)" package="5 mm [THT]"]
  LED11 = LED - 5mm [color="Red (635nm)" package="5 mm [THT]"]
  R1 = Resistor [tolerance=±5% resistance=200 package=THT]
  R2 = Resistor [tolerance=±5% resistance=200 package=THT]
  R3 = Resistor [tolerance=±5% resistance=200 package=THT]
  R4 = Resistor [tolerance=±5% resistance=200 package=THT]
  R5 = Resistor [tolerance=±5% resistance=200 package=THT]
  R6 = Resistor [tolerance=±5% resistance=200 package=THT]
  R7 = Resistor [tolerance=±5% resistance=200 package=THT]
  R8 = Resistor [tolerance=±5% resistance=200 package=THT]
  R9 = Resistor [tolerance=±5% resistance=200 package=THT]
  R10 = Resistor [tolerance=±5% resistance=200 package=THT]
  R11 = Resistor [tolerance=±5% resistance=200 package=THT]
  IC1 = SN74HC595N [package=dil16]
  IC2 = SN74HC595N [package=dil16]
  Part1 = Arduino Uno (Rev3)

nets (from the breadboard view):
  N1: LED1.cathode, IC1.QA
  N2: LED1.anode, R1.Pin_0
  N3: LED2.anode, R2.Pin_0
  N4: LED3.cathode, IC1.QC
  N5: LED3.anode, R3.Pin_0
  N6: LED4.cathode, IC1.QD
  N7: LED4.anode, R4.Pin_0
  N8: LED5.cathode, IC1.QE
  N9: LED5.anode, R5.Pin_0
  N10: LED6.cathode, IC1.QF
  N11: LED6.anode, R6.Pin_0
  N12: LED7.cathode, IC1.QG
  N13: LED7.anode, R7.Pin_0
  N14: LED8.cathode, IC1.QH
  N15: LED8.anode, R8.Pin_0
  N16: LED9.cathode, IC2.QA
  N17: LED9.anode, R9.Pin_0
  N18: LED10.anode, R10.Pin_0
  N19: LED11.cathode, IC2.QC
  N20: LED11.anode, R11.Pin_0
  GND: R1.Pin_1, R2.Pin_1, R3.Pin_1, R4.Pin_1, R5.Pin_1, R6.Pin_1, R7.Pin_1, R8.Pin_1, R9.Pin_1, R10.Pin_1, R11.Pin_1, IC1.GND, IC1.G, IC2.GND, IC2.G, Part1.GND
  N21: IC1.QH*, IC2.SER
  VCC: IC1.SCL, IC1.VCC, IC2.SCL, IC2.VCC, Part1.5V
  N22: IC1.SCK, IC2.SCK, Part1.D12/MISO
  N23: IC1.RCK, IC2.RCK, Part1.D8
  N24: IC1.SER, Part1.D11_PWM/MOSI

notes:
  Clock and latch pins are shared between the ICs. The Q7' pin of IC1 is connected to the DATA pin of IC2.
  Green - Data
  Brown - Latch
  Grey - Clock
  Green jumpers were used for connections between ICs, LEDs and Arduino.
  Yellow wires were used for connections between ICs

custom parts:
  SN74HC595N: 8-bit SHIFT REGISTER, output latch
