# Fritzing sketch Shift_Cascade_Matrix_Backup (saved by Fritzing 0.9.0b)
breadboards: 1

parts:
  8x8_LED_Matrix1 = 8x8 LED Matrix 1388ASR
  R1 = Resistor [tolerance=±5% resistance=200 package=THT]
  R2 = Resistor [tolerance=±5% resistance=200 package=THT]  # not connected
  R3 = Resistor [tolerance=±5% resistance=200 package=THT]
  R4 = Resistor [tolerance=±5% resistance=200 package=THT]
  R5 = Resistor [tolerance=±5% resistance=200 package=THT]
  R6 = Resistor [tolerance=±5% resistance=200 package=THT]
  R7 = Resistor [tolerance=±5% resistance=200 package=THT]
  R8 = Resistor [tolerance=±5% resistance=200 package=THT]
  IC1 = SN74HC595N [package=dil16]
  IC2 = SN74HC595N [package=dil16]
  Part1 = Arduino Uno (Rev3)

nets:
  N1: 8x8_LED_Matrix1.Pin_1, R1.Pin_0
  N2: 8x8_LED_Matrix1.Pin_4, IC2.QC
  N3: 8x8_LED_Matrix1.Pin_5, R3.Pin_0
  N4: 8x8_LED_Matrix1.Pin_6, IC2.QE
  N5: 8x8_LED_Matrix1.Pin_7#7, R5.Pin_0
  N6: 8x8_LED_Matrix1.Pin_8, R4.Pin_0
  N7: 8x8_LED_Matrix1.Pin_9, R6.Pin_1
  N8: 8x8_LED_Matrix1.Pin_7#10, IC2.QD
  N9: 8x8_LED_Matrix1.Pin_11, IC2.QF
  N10: 8x8_LED_Matrix1.Pin_12, R7.Pin_1
  N11: 8x8_LED_Matrix1.Pin_13, IC2.QA
  N12: 8x8_LED_Matrix1.Pin14, R8.Pin_1
  N13: 8x8_LED_Matrix1.Pin_15, IC2.QG
  N14: 8x8_LED_Matrix1.Pin_16, IC2.QH
  N15: R1.Pin_1, IC1.QD
  N16: R3.Pin_1, IC1.QA
  N17: R4.Pin_1, IC1.QF
  N18: R5.Pin_1, IC1.QC
  N19: R6.Pin_0, IC1.QH
  N20: R7.Pin_0, IC1.QE
  N21: R8.Pin_0, IC1.QG
  GND: IC1.GND, IC2.GND
  N22: IC1.QH*, IC2.SER
  VCC: IC1.SCL, IC1.VCC, IC2.SCL, IC2.VCC, Part1.5V
  N23: IC1.SCK, IC2.SCK, Part1.D12/MISO
  N24: IC1.RCK, IC2.RCK, Part1.D8
  N25: IC1.G, IC2.G, Part1.GND
  N26: IC1.SER, Part1.D11_PWM/MOSI

custom parts:
  8x8 LED Matrix 1388ASR: Red Color Common Anode 8x8 LED Matrix
  SN74HC595N: 8-bit SHIFT REGISTER, output latch
